# Fritzing sketch Esp8266 (saved by Fritzing 0.9.2b)
circuit board: 12.926cm x 10.3435cm
breadboards: 2

parts:
  U1 = Optocoupler [package=THT]
  Q1 = Basic FET N-Channel [package="D2Pak [SMD]"]
  R2 = Resistor [tolerance=±5% resistance=10k package=THT]
  70v = Power plug
  BAT1 = Battery Holders [package=battcom_20mm_pth]
  U2 = NodeMCU V1.0
  R3 = Resistor [tolerance=±5% resistance=110 package=THT]
  Led_strip = Power plug

nets:
  N1: U1.Pin_1, R3.Pin_0
  GND: U1.Pin_2, U1.Pin_4, 70v.GND, BAT1.-, U2.GND, Led_strip.GND
  N2: U1.Pin_5, Q1.Gate, R2.Pin_1
  Vcc Led strip: Q1.drain, R2.Pin_0, 70v.VCC
  N3: Q1.source, Led_strip.VCC
  Vcc Esp8266: BAT1.+, U2.Vin
  N4: U2.D1, R3.Pin_1

notes:
  Out to  Led Strip
  Source of Led Strip
  Out to Source Strip

custom parts:
  NodeMCU V1.0: ESP8266 based NodeMCU
