# Fritzing sketch Raspberry Pi (saved by Fritzing 0.9.2b)
breadboards: 1

parts:
  Raspberry_Pi1 = Raspberry Pi 2
  S1 = Pushbutton [package="[THT]"]

nets:
  N1: Raspberry_Pi1.GND, S1.Pin_1, S1.Pin_2
  N2: Raspberry_Pi1.GPIO18, S1.Pin_3, S1.Pin_4
