# Fritzing sketch RaspberryPi (saved by Fritzing 0.9.2b)
breadboards: 1

parts:
  Raspberry_Pi1 = Raspberry Pi 2
  R1 = Resistor [tolerance=±5% resistance=220 package=THT]
  S1 = Pushbutton [package="[SMD]"]

nets:
  3.3v: Raspberry_Pi1.3v3, S1.Pin_1, S1.Pin_2
  N1: Raspberry_Pi1.GPIO18, R1.Pin_0, S1.Pin_3, S1.Pin_4
  GND: Raspberry_Pi1.GND, R1.Pin_1
